# Fritzing sketch 60hz_clock (saved by Fritzing 0.9.2b)
breadboards: 1

parts:
  IC1 = IC, DIP package, 8 pins [chip_label=555 part_number="555 Clock"]
  Power_plug1 = Power plug
  R1 = Resistor [tolerance=±5% resistance=330 package=THT]
  R2 = Resistor [tolerance=±5% resistance=330 package=THT]
  C2 = Ceramic Capacitor [capacitance=10nF package="100 mil [THT, multilayer]"]
  C3 = Ceramic Capacitor [capacitance=22µF package="100 mil [THT, multilayer]"]

nets:
  N1: IC1.pin1, IC1.pin5, Power_plug1.GND, C2.0
  N2: IC1.pin2, IC1.pin6, IC1.pin7, R1.Pin_1, R2.Pin_0, R2.Pin_1, C3.0
  N3: IC1.pin4, IC1.pin8, Power_plug1.VCC, R1.Pin_0
  N4: C2.1, C3.1

notes:
  10nf
  22uf
  Output
